# Fritzing sketch debut conception (saved by Fritzing 0.9.3b)
breadboards: 1

parts:
  Raspberry_Pi1 = Raspberry Pi B+  # not connected
  BAT1 = Battery Holders [package=battery-aa-kit]
  U6 = TRANSCHIPTC5747 [package=camera_sfv24r-2st_2]  # not connected
  F1 = Fan - Ventilador [package=THT]  # not connected
  Composant5 = Arduino Uno (Rev3)
  M6 = Stepper Motor - Bipolar
  M7 = Stepper Motor - Bipolar
  DRV_1 = DRV 8825 Stepper Motor Carrier, High Current [part_number="DRV 8825"]
  DRV_2 = DRV 8825 Stepper Motor Carrier, High Current [part_number="DRV 8825"]
  Composant6 = Arduino Uno (Rev3)
  M8 = Stepper Motor - Bipolar
  M9 = Stepper Motor - Bipolar
  DRV_3 = DRV 8825 Stepper Motor Carrier, High Current [part_number="DRV 8825"]
  DRV_4 = DRV 8825 Stepper Motor Carrier, High Current [part_number="DRV 8825"]
  Composant7 = INA169 Current Sensor Breakout [part_number=BOB-12040]

nets:
  N1: BAT1.+, DRV_1.VOLTAGE_ST/_MT, DRV_3.VOLTAGE_ST/_MT, DRV_4.VOLTAGE_ST/_MT, Composant7.VIN+
  GND: BAT1.-, Composant5.GND, DRV_1.GROUND_ST/_MT, DRV_2.GROUND_ST/_MT, DRV_3.GROUND_ST/_MT, DRV_4.GROUND_ST/_MT, Composant7.GND
  N2: Composant5.A1, Composant7.VOUT
  N3: Composant5.D13/SCK, DRV_1.ENABLE, DRV_2.ENABLE
  N4: Composant5.D2, DRV_1.SLEEP
  N5: Composant5.D3_PWM, DRV_2.STEP
  N6: Composant5.D5_PWM, DRV_1.DIRECTION
  N7: Composant5.D6_PWM, DRV_2.DIRECTION
  5V: Composant5.5V, DRV_1.VOLTAGE_DD, DRV_2.VOLTAGE_DD, Composant7.VCC
  N8: M6.A, DRV_1.OUT_2B
  N9: M6.C, DRV_1.OUT_2A
  N10: M6.B, DRV_1.OUT_1A
  N11: M6.D, DRV_1.OUT_1B
  N12: M7.A, DRV_2.OUT_2B
  N13: M7.C, DRV_2.OUT_2A
  N14: M7.B, DRV_2.OUT_1A
  N15: M7.D, DRV_2.OUT_1B
  N16: DRV_2.VOLTAGE_ST/_MT, Composant7.VIN-
  N17: Composant6.D13/SCK, DRV_3.ENABLE, DRV_4.ENABLE
  N18: Composant6.D2, DRV_3.SLEEP
  N19: Composant6.D3_PWM, DRV_4.STEP
  N20: Composant6.D5_PWM, DRV_3.DIRECTION
  N21: Composant6.D6_PWM, DRV_4.DIRECTION
  N22: Composant6.5V, DRV_3.VOLTAGE_DD, DRV_4.VOLTAGE_DD
  N23: M8.A, DRV_3.OUT_2B
  N24: M8.C, DRV_3.OUT_2A
  N25: M8.B, DRV_3.OUT_1A
  N26: M8.D, DRV_3.OUT_1B
  N27: M9.A, DRV_4.OUT_2B
  N28: M9.C, DRV_4.OUT_2A
  N29: M9.B, DRV_4.OUT_1A
  N30: M9.D, DRV_4.OUT_1B

custom parts:
  Fan - Ventilador: Ventilador de 2 pines, se encuentra comunmente en computadoras de escritorio
  INA169 Current Sensor Breakout: INA169 Current Sensor Breakout Board
