# Fritzing sketch RoDeP-elec (saved by Fritzing 0.9.3b)
breadboards: 1

parts:
  Raspberry_Pi1 = Raspberry Pi B+
  Composant5 = Arduino Uno (Rev3)
  M6 = Stepper Motor - Bipolar
  M7 = Stepper Motor - Bipolar
  DRV_1 = DRV 8825 Stepper Motor Carrier, High Current [part_number="DRV 8825"]
  DRV_2 = DRV 8825 Stepper Motor Carrier, High Current [part_number="DRV 8825"]
  Composant6 = Arduino Uno (Rev3)
  M8 = Stepper Motor - Bipolar
  M9 = Stepper Motor - Bipolar
  DRV_3 = DRV 8825 Stepper Motor Carrier, High Current [part_number="DRV 8825"]
  DRV_4 = DRV 8825 Stepper Motor Carrier, High Current [part_number="DRV 8825"]
  USBTTL1 = USB A Plug
  USBTTL2 = USB A Plug
  USBTTL3 = USB A Plug
  USBTTL4 = USB A Plug
  VCC1 = Battery
  HLK-PM1 = HLK-PM01
  U1 = SWITCH_SPDT [package=kps-1290]
  U2 = SWITCH_SPDT [package=kps-1290]
  U3 = SWITCH_SPDT [package=kps-1290]

nets:
  N1: Raspberry_Pi1.GND, HLK-PM1.-Vo
  N2: Raspberry_Pi1.5V, HLK-PM1.+Vo
  N3: Composant5.D9_PWM, U2.O
  N4: Composant5.D10_PWM/SS, U3.O
  N5: Composant5.D13/SCK, DRV_1.ENABLE, DRV_2.ENABLE
  N6: Composant5.GND, U2.S
  N7: Composant5.D2, DRV_1.SLEEP
  N8: Composant5.D3_PWM, DRV_2.STEP
  N9: Composant5.D5_PWM, DRV_1.DIRECTION
  N10: Composant5.D6_PWM, DRV_2.DIRECTION
  N11: Composant5.5V, DRV_2.VOLTAGE_DD
  N12: M6.A, DRV_1.OUT_2B
  N13: M6.C, DRV_1.OUT_2A
  N14: M6.B, DRV_1.OUT_1A
  N15: M6.D, DRV_1.OUT_1B
  N16: M7.A, DRV_2.OUT_2B
  N17: M7.C, DRV_2.OUT_2A
  N18: M7.B, DRV_2.OUT_1A
  N19: M7.D, DRV_2.OUT_1B
  N20: DRV_1.VOLTAGE_ST/_MT, DRV_2.VOLTAGE_ST/_MT, DRV_3.VOLTAGE_ST/_MT, DRV_4.GROUND_ST/_MT, HLK-PM1.AC#0, U1.S
  N21: DRV_1.GROUND_ST/_MT, DRV_2.GROUND_ST/_MT, DRV_3.GROUND_ST/_MT, DRV_4.VOLTAGE_ST/_MT, VCC1.-, HLK-PM1.AC#1
  N22: Composant6.D13/SCK, DRV_3.ENABLE, DRV_4.ENABLE
  N23: Composant6.D2, DRV_3.SLEEP
  N24: Composant6.D3_PWM, DRV_4.STEP
  N25: Composant6.D5_PWM, DRV_3.DIRECTION
  N26: Composant6.D6_PWM, DRV_4.DIRECTION
  N27: Composant6.5V, DRV_4.VOLTAGE_DD
  N28: M8.A, DRV_3.OUT_2B
  N29: M8.C, DRV_3.OUT_2A
  N30: M8.B, DRV_3.OUT_1A
  N31: M8.D, DRV_3.OUT_1B
  N32: M9.A, DRV_4.OUT_2B
  N33: M9.C, DRV_4.OUT_2A
  N34: M9.B, DRV_4.OUT_1A
  N35: M9.D, DRV_4.OUT_1B
  N36: USBTTL1.usb, USBTTL3.usb
  N37: USBTTL2.usb, USBTTL4.usb
  N38: VCC1.+, U1.O
